# Fritzing sketch adapter (saved by Fritzing 0.7.12b)
breadboards: 1
perfboards: 1

parts:
  R1 = Resistor [tolerance=±5% resistance=180 package=THT]
  J1 = double row female pin header, 4 pins [form="♀ (female)"]
  LED1 = LED - 5mm [color="Infrared (880nm)" package="5 mm [THT]"]
  LED2 = LED - 5mm [color="Red (633nm)" package="5 mm [THT]"]
  R2 = Resistor [tolerance=±5% resistance=10k package=THT]

nets:
  N1: R1.Pin_0, LED1.anode
  N2: R1.Pin_1, J1.pin4
  N3: J1.pin1, R2.Pin_1
  N4: J1.pin2, LED1.cathode
  N5: J1.pin3, LED2.cathode
  N6: LED2.anode, R2.Pin_0

notes:
  GND
  3V3
  TX
